// Logisim project clock.circ as structural Verilog: 6 circuits, main circuit main
module main (
  output [3:0] out_1,
  output [3:0] out_2,
  output [3:0] out_3,
  output [3:0] out_4,
  output [3:0] out_5,
  output [3:0] out_6
);

  wire button_1_out, n4bit7segmentdecoder_1_a, n4bit7segmentdecoder_1_b, n4bit7segmentdecoder_1_f,
       n4bit7segmentdecoder_1_g, n4bit7segmentdecoder_2_c, n4bit7segmentdecoder_2_d,
       n4bit7segmentdecoder_2_e, n4bit7segmentdecoder_2_p, n4bit7segmentdecoder_3_a,
       n4bit7segmentdecoder_3_b, n4bit7segmentdecoder_3_f, n4bit7segmentdecoder_3_g,
       n4bit7segmentdecoder_4_c, n4bit7segmentdecoder_4_d, n4bit7segmentdecoder_4_e,
       n4bit7segmentdecoder_4_p, n4bit7segmentdecoder_5_a, n4bit7segmentdecoder_5_b,
       n4bit7segmentdecoder_5_f, n4bit7segmentdecoder_5_g, n4bit7segmentdecoder_6_c,
       n4bit7segmentdecoder_6_d, n4bit7segmentdecoder_6_e, n4bit7segmentdecoder_6_p,
       n4bit7segmentdecoder_7_a, n4bit7segmentdecoder_7_b, n4bit7segmentdecoder_7_f,
       n4bit7segmentdecoder_7_g, n4bit7segmentdecoder_8_c, n4bit7segmentdecoder_8_d,
       n4bit7segmentdecoder_8_e, n4bit7segmentdecoder_8_p, n4bit7segmentdecoder_9_a,
       n4bit7segmentdecoder_9_b, n4bit7segmentdecoder_9_f, n4bit7segmentdecoder_9_g,
       n4bit7segmentdecoder_10_c, n4bit7segmentdecoder_10_d, n4bit7segmentdecoder_10_e,
       n4bit7segmentdecoder_10_p, n4bit7segmentdecoder_11_a, n4bit7segmentdecoder_11_b,
       n4bit7segmentdecoder_11_f, n4bit7segmentdecoder_11_g, n4bit7segmentdecoder_12_c,
       n4bit7segmentdecoder_12_d, n4bit7segmentdecoder_12_e, n4bit7segmentdecoder_12_p;
  wire [15:0] time_1_t;

  Button button_1 (.out(button_1_out));
  Time time_1 (.T(time_1_t), .DEL(button_1_out));
  Hours hours_1 (.T(time_1_t), .HE(out_2), .HT(out_1));
  Minutes minutes_1 (.T(time_1_t), .MT(out_3), .ME(out_4));
  Seconds seconds_1 (.T(time_1_t), .ST(out_5), .SE(out_6));
  _4bit7SegmentDecoder u_4bit7segmentdecoder_1 (
    .N(out_1), .a(n4bit7segmentdecoder_1_a), .b(n4bit7segmentdecoder_1_b), .f(n4bit7segmentdecoder_1_f),
    .g(n4bit7segmentdecoder_1_g));  // open: Point, c, d, e, p
  _7_Segment_Display u_7_segment_display_1 (
    .g(n4bit7segmentdecoder_1_f), .f(n4bit7segmentdecoder_1_g), .a(n4bit7segmentdecoder_1_a),
    .b(n4bit7segmentdecoder_1_b), .e(n4bit7segmentdecoder_2_e), .d(n4bit7segmentdecoder_2_d),
    .c(n4bit7segmentdecoder_2_c), .dp(n4bit7segmentdecoder_2_p));
  _4bit7SegmentDecoder u_4bit7segmentdecoder_2 (
    .N(out_1), .c(n4bit7segmentdecoder_2_c), .d(n4bit7segmentdecoder_2_d), .e(n4bit7segmentdecoder_2_e),
    .p(n4bit7segmentdecoder_2_p));  // open: Point, a, b, f, g
  _4bit7SegmentDecoder u_4bit7segmentdecoder_3 (
    .N(out_2), .a(n4bit7segmentdecoder_3_a), .b(n4bit7segmentdecoder_3_b), .f(n4bit7segmentdecoder_3_f),
    .g(n4bit7segmentdecoder_3_g));  // open: Point, c, d, e, p
  _7_Segment_Display u_7_segment_display_2 (
    .g(n4bit7segmentdecoder_3_f), .f(n4bit7segmentdecoder_3_g), .a(n4bit7segmentdecoder_3_a),
    .b(n4bit7segmentdecoder_3_b), .e(n4bit7segmentdecoder_4_e), .d(n4bit7segmentdecoder_4_d),
    .c(n4bit7segmentdecoder_4_c), .dp(n4bit7segmentdecoder_4_p));
  _4bit7SegmentDecoder u_4bit7segmentdecoder_4 (
    .N(out_2), .c(n4bit7segmentdecoder_4_c), .d(n4bit7segmentdecoder_4_d), .e(n4bit7segmentdecoder_4_e),
    .p(n4bit7segmentdecoder_4_p));  // open: Point, a, b, f, g
  _4bit7SegmentDecoder u_4bit7segmentdecoder_5 (
    .N(out_3), .a(n4bit7segmentdecoder_5_a), .b(n4bit7segmentdecoder_5_b), .f(n4bit7segmentdecoder_5_f),
    .g(n4bit7segmentdecoder_5_g));  // open: Point, c, d, e, p
  _7_Segment_Display u_7_segment_display_3 (
    .g(n4bit7segmentdecoder_5_f), .f(n4bit7segmentdecoder_5_g), .a(n4bit7segmentdecoder_5_a),
    .b(n4bit7segmentdecoder_5_b), .e(n4bit7segmentdecoder_6_e), .d(n4bit7segmentdecoder_6_d),
    .c(n4bit7segmentdecoder_6_c), .dp(n4bit7segmentdecoder_6_p));
  _4bit7SegmentDecoder u_4bit7segmentdecoder_6 (
    .N(out_3), .c(n4bit7segmentdecoder_6_c), .d(n4bit7segmentdecoder_6_d), .e(n4bit7segmentdecoder_6_e),
    .p(n4bit7segmentdecoder_6_p));  // open: Point, a, b, f, g
  _4bit7SegmentDecoder u_4bit7segmentdecoder_7 (
    .N(out_4), .a(n4bit7segmentdecoder_7_a), .b(n4bit7segmentdecoder_7_b), .f(n4bit7segmentdecoder_7_f),
    .g(n4bit7segmentdecoder_7_g));  // open: Point, c, d, e, p
  _7_Segment_Display u_7_segment_display_4 (
    .g(n4bit7segmentdecoder_7_f), .f(n4bit7segmentdecoder_7_g), .a(n4bit7segmentdecoder_7_a),
    .b(n4bit7segmentdecoder_7_b), .e(n4bit7segmentdecoder_8_e), .d(n4bit7segmentdecoder_8_d),
    .c(n4bit7segmentdecoder_8_c), .dp(n4bit7segmentdecoder_8_p));
  _4bit7SegmentDecoder u_4bit7segmentdecoder_8 (
    .N(out_4), .c(n4bit7segmentdecoder_8_c), .d(n4bit7segmentdecoder_8_d), .e(n4bit7segmentdecoder_8_e),
    .p(n4bit7segmentdecoder_8_p));  // open: Point, a, b, f, g
  _4bit7SegmentDecoder u_4bit7segmentdecoder_9 (
    .N(out_5), .a(n4bit7segmentdecoder_9_a), .b(n4bit7segmentdecoder_9_b), .f(n4bit7segmentdecoder_9_f),
    .g(n4bit7segmentdecoder_9_g));  // open: Point, c, d, e, p
  _7_Segment_Display u_7_segment_display_5 (
    .g(n4bit7segmentdecoder_9_f), .f(n4bit7segmentdecoder_9_g), .a(n4bit7segmentdecoder_9_a),
    .b(n4bit7segmentdecoder_9_b), .e(n4bit7segmentdecoder_10_e), .d(n4bit7segmentdecoder_10_d),
    .c(n4bit7segmentdecoder_10_c), .dp(n4bit7segmentdecoder_10_p));
  _4bit7SegmentDecoder u_4bit7segmentdecoder_10 (
    .N(out_5), .c(n4bit7segmentdecoder_10_c), .d(n4bit7segmentdecoder_10_d), .e(n4bit7segmentdecoder_10_e),
    .p(n4bit7segmentdecoder_10_p));  // open: Point, a, b, f, g
  _4bit7SegmentDecoder u_4bit7segmentdecoder_11 (
    .N(out_6), .a(n4bit7segmentdecoder_11_a), .b(n4bit7segmentdecoder_11_b), .f(n4bit7segmentdecoder_11_f),
    .g(n4bit7segmentdecoder_11_g));  // open: Point, c, d, e, p
  _7_Segment_Display u_7_segment_display_6 (
    .g(n4bit7segmentdecoder_11_f), .f(n4bit7segmentdecoder_11_g), .a(n4bit7segmentdecoder_11_a),
    .b(n4bit7segmentdecoder_11_b), .e(n4bit7segmentdecoder_12_e), .d(n4bit7segmentdecoder_12_d),
    .c(n4bit7segmentdecoder_12_c), .dp(n4bit7segmentdecoder_12_p));
  _4bit7SegmentDecoder u_4bit7segmentdecoder_12 (
    .N(out_6), .c(n4bit7segmentdecoder_12_c), .d(n4bit7segmentdecoder_12_d), .e(n4bit7segmentdecoder_12_e),
    .p(n4bit7segmentdecoder_12_p));  // open: Point, a, b, f, g
endmodule

module Hours (
  input  [15:0] T,
  output [3:0] HT,
  output [3:0] HE
);

  wire [15:0] divider_1_out, divider_2_out, divider_3_rem, divider_4_out, divider_4_rem;

  Divider #(.width(16)) divider_1 (.a(T), .b(16'h3c), .out(divider_1_out));  // open: upper, rem
  Divider #(.width(16)) divider_2 (.a(divider_1_out), .b(16'h3c), .out(divider_2_out));  // open: upper, rem
  Divider #(.width(16)) divider_3 (.a(divider_2_out), .b(16'h18), .rem(divider_3_rem));  // open: out, upper
  Divider #(.width(16)) divider_4 (
    .a(divider_3_rem), .b(16'ha), .out(divider_4_out), .rem(divider_4_rem));  // open: upper
  Bit_Extender #(.in_width(16), .out_width(4)) bit_extender_1 (.in(divider_4_out), .out(HT));
  Bit_Extender #(.in_width(16), .out_width(4)) bit_extender_2 (.in(divider_4_rem), .out(HE));
endmodule

module Time (
  input  DEL,
  output [15:0] T
);

  wire clock_1_out;
  wire [15:0] adder_1_out, bit_extender_1_out;

  Clock clock_1 (.out(clock_1_out));
  assign bit_extender_1_out = {{15{1'b0}}, clock_1_out};  // Bit_Extender bit_extender_1
  Adder #(.width(16)) adder_1 (.a(T), .b(bit_extender_1_out), .out(adder_1_out));  // open: cin, cout
  Register #(.width(16), .trigger("falling")) register_1 (
    .D(adder_1_out), .Q(T), .clk(clock_1_out), .clr(DEL));  // open: en
endmodule

module Minutes (
  input  [15:0] T,
  output [3:0] MT,
  output [3:0] ME
);

  wire [15:0] divider_1_out, divider_2_rem, divider_3_out, divider_3_rem;

  Divider #(.width(16)) divider_1 (.a(T), .b(16'h3c), .out(divider_1_out));  // open: upper, rem
  Divider #(.width(16)) divider_2 (.a(divider_1_out), .b(16'h3c), .rem(divider_2_rem));  // open: out, upper
  Divider #(.width(16)) divider_3 (
    .a(divider_2_rem), .b(16'ha), .out(divider_3_out), .rem(divider_3_rem));  // open: upper
  Bit_Extender #(.in_width(16), .out_width(4)) bit_extender_1 (.in(divider_3_out), .out(MT));
  Bit_Extender #(.in_width(16), .out_width(4)) bit_extender_2 (.in(divider_3_rem), .out(ME));
endmodule

module Seconds (
  input  [15:0] T,
  output [3:0] ST,
  output [3:0] SE
);

  wire [15:0] divider_1_rem, divider_2_out, divider_2_rem;

  Divider #(.width(16)) divider_1 (.a(T), .b(16'h3c), .rem(divider_1_rem));  // open: out, upper
  Divider #(.width(16)) divider_2 (
    .a(divider_1_rem), .b(16'ha), .out(divider_2_out), .rem(divider_2_rem));  // open: upper
  Bit_Extender #(.in_width(16), .out_width(4)) bit_extender_1 (.in(divider_2_out), .out(ST));
  Bit_Extender #(.in_width(16), .out_width(4)) bit_extender_2 (.in(divider_2_rem), .out(SE));
endmodule

module _4bit7SegmentDecoder (
  input  Point,
  input  [3:0] N,
  output a,
  output b,
  output c,
  output d,
  output e,
  output f,
  output g,
  output p
);

  wire _0_out, _1_out, _2_out, _3_out, _4_out, _5_out, _6_out, _7_out, _8_out, _9_out, not_1_out, not_2_out,
       not_3_out, not_4_out, not_5_out, not_6_out, not_7_out, not_8_out, not_9_out, not_10_out, not_11_out,
       not_12_out, not_13_out;

  Hex_Digit_Display hex_digit_display_1 (.value(N), .dp(Point));
  not not_1 (not_1_out, N[0]);
  not not_2 (not_2_out, N[1]);
  not not_3 (not_3_out, N[2]);
  not not_4 (not_4_out, N[3]);
  not not_5 (not_5_out, N[2]);
  not not_6 (not_6_out, N[1]);
  not not_7 (not_7_out, N[3]);
  not not_8 (not_8_out, N[0]);
  not not_9 (not_9_out, N[3]);
  not not_10 (not_10_out, N[3]);
  not not_11 (not_11_out, N[3]);
  not not_12 (not_12_out, N[1]);
  not not_13 (not_13_out, N[2]);
  nor _0 (_0_out, N[0], N[1], N[2], N[3]);
  nor _1 (_1_out, not_1_out, N[1], N[2], N[3]);
  nor _2 (_2_out, N[0], not_2_out, N[2], N[3]);
  and _3 (_3_out, N[0], N[1], not_3_out, not_4_out);
  nor _4 (_4_out, N[0], N[1], not_5_out, N[3]);
  and _5 (_5_out, N[0], not_6_out, N[2], not_7_out);
  and _6 (_6_out, not_8_out, N[1], N[2], not_9_out);
  and _7 (_7_out, N[0], N[1], N[2], not_10_out);
  nor _8 (_8_out, N[0], N[1], N[2], not_11_out);
  and _9 (_9_out, N[0], not_12_out, not_13_out, N[3]);
  or or_1 (a, _0_out, _2_out, _3_out, _5_out, _6_out, _7_out, _8_out, _9_out);
  or or_2 (b, _0_out, _1_out, _2_out, _3_out, _4_out, _7_out, _8_out, _9_out);
  or or_3 (c, _0_out, _1_out, _3_out, _4_out, _5_out, _6_out, _7_out, _8_out, _9_out);
  or or_4 (d, _0_out, _2_out, _3_out, _5_out, _6_out, _8_out, _9_out);
  or or_5 (e, _0_out, _2_out, _6_out, _8_out);
  or or_6 (f, _2_out, _3_out, _4_out, _5_out, _6_out, _8_out, _9_out);
  or or_7 (g, _0_out, _4_out, _5_out, _6_out, _8_out, _9_out);
  _7_Segment_Display u_7_segment_display_1 (.g(f), .f(g), .a(a), .b(b), .e(e), .d(d), .c(c), .dp(Point));

  assign p = Point;
endmodule
